// Digital circuit Template2.dig as structural Verilog
module Template2 (
  input  A,
  input  B,
  input  C,
  input  D,
  output Z1,
  output Z2,
  output Z3
);

  wire and_1_out, and_2_out, and_3_out, and_4_out, and_5_out, and_6_out, and_7_out, and_8_out, and_9_out,
       and_10_out, not_1_out, not_2_out, not_3_out, not_4_out, not_5_out, not_6_out, not_7_out, not_8_out,
       not_9_out, not_10_out, not_11_out, not_12_out, not_13_out, not_14_out, not_15_out, not_16_out,
       not_17_out, not_18_out;

  not not_1 (not_1_out, C);
  not not_2 (not_2_out, A);
  not not_3 (not_3_out, C);
  not not_4 (not_4_out, D);
  not not_5 (not_5_out, D);
  not not_6 (not_6_out, A);
  not not_7 (not_7_out, A);
  not not_8 (not_8_out, B);
  not not_9 (not_9_out, C);
  not not_10 (not_10_out, B);
  and and_1 (and_1_out, A, not_1_out);
  and and_2 (and_2_out, not_2_out, B, not_3_out, not_4_out);
  and and_3 (and_3_out, A, B, C, not_5_out);
  and and_4 (and_4_out, not_6_out, C);
  and and_5 (and_5_out, not_7_out, not_8_out, not_9_out, D);
  and and_6 (and_6_out, A, not_10_out, C, D);
  not not_11 (not_11_out, A);
  not not_12 (not_12_out, B);
  not not_13 (not_13_out, C);
  not not_14 (not_14_out, D);
  not not_15 (not_15_out, A);
  not not_16 (not_16_out, C);
  not not_17 (not_17_out, B);
  not not_18 (not_18_out, D);
  and and_7 (and_7_out, not_11_out, not_12_out, not_13_out, not_14_out);
  and and_8 (and_8_out, not_15_out, B, not_16_out, D);
  and and_9 (and_9_out, A, not_17_out, C, not_18_out);
  and and_10 (and_10_out, A, B, C, D);
  or or_1 (Z1, and_1_out, and_2_out, and_3_out);
  or or_2 (Z2, and_4_out, and_5_out, and_6_out);
  or or_3 (Z3, and_7_out, and_8_out, and_9_out, and_10_out);
endmodule
