// Digital circuit Template2.dig as structural Verilog
module Template2 (
  input  X0,
  input  X1,
  input  Selector,
  output Z
);

  wire not_1_out, or_1_out, or_2_out;

  or or_1 (or_1_out, X0, Selector);
  or or_2 (or_2_out, X1, not_1_out);
  not not_1 (not_1_out, Selector);
  and and_1 (Z, or_1_out, or_2_out);
endmodule
