// Digital circuit Template-01.dig as structural Verilog
module Template_01 (
  input  [3:0] In,
  output A,
  output B,
  output C,
  output D,
  output E,
  output F,
  output G
);

  wire and_1_out, and_2_out, and_3_out, and_4_out, and_5_out, and_6_out, and_7_out, and_8_out, and_9_out,
       and_10_out, and_11_out, and_12_out, and_13_out, and_14_out, and_15_out, and_16_out, and_17_out,
       and_18_out, and_19_out, and_20_out, and_21_out, and_22_out, and_23_out, not_1_out, not_2_out,
       not_3_out, not_4_out, not_5_out, not_6_out, not_7_out, not_8_out, not_9_out, not_10_out, not_11_out,
       not_12_out, not_13_out, not_14_out, not_15_out, not_16_out, not_17_out, not_18_out, not_19_out,
       not_20_out, not_21_out, not_22_out, not_23_out, not_24_out, not_25_out, not_26_out, not_27_out;

  and and_1 (and_1_out, In[2], In[1], In[0]);
  and and_2 (and_2_out, not_1_out, In[1]);
  not not_1 (not_1_out, In[2]);
  and and_3 (and_3_out, In[2], not_2_out, In[0]);
  not not_2 (not_2_out, In[1]);
  and and_4 (and_4_out, not_3_out, not_4_out);
  not not_3 (not_3_out, In[2]);
  not not_4 (not_4_out, In[0]);
  and and_5 (and_5_out, In[2], In[1], not_5_out);
  not not_5 (not_5_out, In[0]);
  and and_6 (and_6_out, not_6_out, In[0]);
  not not_6 (not_6_out, In[2]);
  and and_7 (and_7_out, not_7_out, not_8_out);
  not not_7 (not_7_out, In[1]);
  not not_8 (not_8_out, In[0]);
  and and_8 (and_8_out, not_9_out, not_10_out);
  not not_9 (not_9_out, In[2]);
  not not_10 (not_10_out, In[0]);
  and and_9 (and_9_out, In[2], In[1], In[0]);
  and and_10 (and_10_out, not_11_out, not_12_out);
  not not_11 (not_11_out, In[1]);
  not not_12 (not_12_out, In[0]);
  and and_11 (and_11_out, In[2], In[1], not_13_out);
  not not_13 (not_13_out, In[0]);
  and and_12 (and_12_out, not_14_out, In[1]);
  not not_14 (not_14_out, In[2]);
  and and_13 (and_13_out, In[2], not_15_out, In[0]);
  not not_15 (not_15_out, In[1]);
  and and_14 (and_14_out, not_16_out, not_17_out);
  not not_16 (not_16_out, In[2]);
  not not_17 (not_17_out, In[0]);
  and and_15 (and_15_out, In[2], In[1], not_18_out);
  not not_18 (not_18_out, In[0]);
  and and_16 (and_16_out, not_19_out, not_20_out);
  not not_19 (not_19_out, In[2]);
  not not_20 (not_20_out, In[0]);
  and and_17 (and_17_out, In[2], In[1], not_21_out);
  not not_21 (not_21_out, In[0]);
  and and_18 (and_18_out, In[2], In[0]);
  and and_19 (and_19_out, not_22_out, not_23_out);
  not not_22 (not_22_out, In[1]);
  not not_23 (not_23_out, In[0]);
  and and_20 (and_20_out, In[2], In[1], not_24_out);
  not not_24 (not_24_out, In[0]);
  and and_21 (and_21_out, In[2], In[1], not_25_out);
  not not_25 (not_25_out, In[0]);
  and and_22 (and_22_out, In[2], not_26_out);
  not not_26 (not_26_out, In[1]);
  and and_23 (and_23_out, not_27_out, In[1]);
  not not_27 (not_27_out, In[2]);
  or or_1 (E, and_16_out, and_17_out);
  or or_2 (A, and_1_out, and_2_out, and_3_out, and_4_out, and_5_out, In[3]);
  or or_3 (B, and_6_out, and_7_out, and_8_out, and_9_out);
  or or_4 (C, and_10_out, and_11_out, In[0]);
  or or_5 (D, and_12_out, and_13_out, and_14_out, and_15_out, In[3]);
  or or_6 (F, and_18_out, and_19_out, and_20_out, In[3]);
  or or_7 (G, and_21_out, In[3], and_22_out, and_23_out);

  // Other names for the same wires on the sheet: I3 = In[0]; I2 = In[1]; I1 = In[2]; I0 = In[3]
endmodule
