// Digital circuit Template-02.dig as structural Verilog
module Template_02 (
  input  [2:0] In,
  input  clk,
  output [7:0] Z
);

  wire not_1_out, not_2_out, not_3_out, not_4_out, not_5_out, not_6_out, not_7_out, not_8_out, not_9_out,
       not_10_out, not_11_out, not_12_out;
  wire [7:0] and_9_out, and_10_out, and_11_out, and_12_out, and_13_out, and_14_out, and_15_out, and_16_out;
  wire [7:7] and_1_out, and_2_out, and_3_out, and_4_out, and_5_out, and_6_out, and_7_out, and_8_out;

  and and_1 (and_1_out[7], not_1_out, not_2_out, not_3_out);
  not not_1 (not_1_out, In[0]);
  not not_2 (not_2_out, In[1]);
  not not_3 (not_3_out, In[2]);
  and and_2 (and_2_out[7], In[0], not_4_out, not_5_out);
  not not_4 (not_4_out, In[1]);
  not not_5 (not_5_out, In[2]);
  and and_3 (and_3_out[7], not_6_out, In[1], not_7_out);
  not not_6 (not_6_out, In[0]);
  not not_7 (not_7_out, In[2]);
  and and_4 (and_4_out[7], In[0], In[1], not_8_out);
  not not_8 (not_8_out, In[2]);
  and and_5 (and_5_out[7], not_9_out, not_10_out, In[2]);
  not not_9 (not_9_out, In[0]);
  not not_10 (not_10_out, In[1]);
  and and_6 (and_6_out[7], In[0], not_11_out, In[2]);
  not not_11 (not_11_out, In[1]);
  and and_7 (and_7_out[7], not_12_out, In[1], In[2]);
  not not_12 (not_12_out, In[0]);
  and and_8 (and_8_out[7], In[0], In[1], In[2]);
  assign and_9_out = {8{and_1_out[7]}} & 8'h44;  // And and_9, 8 bits wide
  assign and_10_out = {8{and_2_out[7]}} & 8'h69;  // And and_10, 8 bits wide
  assign and_11_out = {8{and_3_out[7]}} & 8'h67;  // And and_11, 8 bits wide
  assign and_12_out = {8{and_4_out[7]}} & 8'h4c;  // And and_12, 8 bits wide
  assign and_13_out = {8{and_5_out[7]}} & 8'h6f;  // And and_13, 8 bits wide
  assign and_14_out = {8{and_6_out[7]}} & 8'h4c;  // And and_14, 8 bits wide
  assign and_15_out = {8{and_7_out[7]}} & 8'h61;  // And and_15, 8 bits wide
  assign and_16_out = {8{and_8_out[7]}} & 8'h62;  // And and_16, 8 bits wide
  assign Z = and_9_out | and_10_out | and_11_out | and_12_out | and_13_out | and_14_out | and_15_out | and_16_out;  // Or or_1, 8 bits wide
  Terminal terminal_1 (.D(Z), .C(clk), .en(1'b1));

  // Other names for the same wires on the sheet: I0 = In[0]; I1 = In[1]; I2 = In[2]
endmodule
