// Digital circuit Template-03.dig as structural Verilog
module Template_03 (
  input  [3:0] In,
  input  [1:0] Selector,
  output [3:0] Output,
  output [3:0] out_4
);

  wire add_1_c_o, add_2_c_o, add_3_c_o, add_4_c_o, and_1_out, and_2_out, and_3_out, and_4_out, and_5_out,
       and_6_out, and_7_out, and_8_out, and_9_out, and_10_out, and_11_out, not_1_out, not_2_out, not_3_out,
       not_4_out, not_5_out, not_6_out, not_7_out, not_8_out, not_9_out, not_10_out, or_1_out, or_2_out;
  wire [2:0] Cyclic;
  wire [3:0] Excess3;
  wire [3:1] _2421;

  or or_1 (or_1_out, In[0], In[1]);
  not not_1 (not_1_out, In[2]);
  not not_2 (not_2_out, In[1]);
  not not_3 (not_3_out, In[1]);
  not not_4 (not_4_out, In[0]);
  and and_1 (and_1_out, In[2], not_5_out, In[0]);
  not not_5 (not_5_out, In[1]);
  and and_2 (and_2_out, In[1], not_6_out);
  not not_6 (not_6_out, In[0]);
  and and_3 (and_3_out, not_7_out, not_8_out, In[0]);
  not not_7 (not_7_out, In[2]);
  not not_8 (not_8_out, In[1]);
  and and_4 (and_4_out, not_9_out, In[2], not_10_out);
  not not_9 (not_9_out, In[3]);
  not not_10 (not_10_out, In[0]);
  and and_5 (and_5_out, In[2], In[1]);
  or or_2 (or_2_out, In[1], In[2]);
  and and_6 (and_6_out, not_1_out, In[1]);
  and and_7 (and_7_out, In[2], not_2_out, In[0]);
  and and_8 (and_8_out, In[2], not_3_out, not_4_out);
  and and_9 (and_9_out, In[2], In[1]);
  and and_10 (and_10_out, or_1_out, In[2]);
  and and_11 (and_11_out, or_2_out, In[0]);
  Add add_1 (.a(In[0]), .b(1'b1), .c_i(1'b0), .s(Excess3[0]), .c_o(add_1_c_o));
  xor xor_1 (Cyclic[0], In[0], In[1]);
  xor xor_2 (Cyclic[1], In[1], In[2]);
  xor xor_3 (Cyclic[2], In[2], In[3]);
  or or_3 (_2421[1], and_6_out, and_7_out, In[3]);
  or or_4 (_2421[2], and_8_out, and_9_out, In[3]);
  or or_5 (_2421[3], and_10_out, In[3]);
  or or_6 (out_4[1], and_1_out, and_2_out, In[3]);
  or or_7 (out_4[2], and_3_out, and_4_out, and_5_out);
  or or_8 (out_4[3], and_11_out, In[3]);
  Add add_2 (.a(In[1]), .b(1'b1), .c_i(add_1_c_o), .s(Excess3[1]), .c_o(add_2_c_o));
  Add add_3 (.a(In[2]), .b(1'b0), .c_i(add_2_c_o), .s(Excess3[2]), .c_o(add_3_c_o));
  Add add_4 (.a(In[3]), .b(1'b0), .c_i(add_3_c_o), .s(Excess3[3]), .c_o(add_4_c_o));
  Multiplexer #(.Selector_Bits(2), .Bits(4)) multiplexer_1 (
    .sel(Selector), .in_0(Excess3), .in_1({In[3], Cyclic}), .in_2({_2421, In[0]}),
    .in_3({out_4[3:1], In[0]}), .out(Output));

  assign out_4[0] = In[0];
  // also tied to GND on the sheet: add_4_c_o

  // Other names for the same wires on the sheet: _642_3[3:0] = {out_4[3:1], In[0]}; _2421[0] = In[0]; I0 = In[0];
  //   I1 = In[1]; I2 = In[2]; Cyclic[3] = In[3]; I3 = In[3]
endmodule
