// Digital circuit Template-04.dig as structural Verilog
module Template_04 (
  input  [6:0] In,
  output [6:0] Output
);

  wire [2:0] xor_3_out;
  wire [6:0] decoder_1_out_1;

  xor xor_1 (xor_3_out[2], In[3], In[2], In[1], In[0]);
  xor xor_2 (xor_3_out[1], In[5], In[4], In[1], In[0]);
  xor xor_3 (xor_3_out[0], In[6], In[4], In[2], In[0]);
  Decoder #(.Selector_Bits(3)) decoder_1 (
    .sel(xor_3_out), .out_1(decoder_1_out_1[6]), .out_2(decoder_1_out_1[5]), .out_3(decoder_1_out_1[4]),
    .out_4(decoder_1_out_1[3]), .out_5(decoder_1_out_1[2]), .out_6(decoder_1_out_1[1]),
    .out_7(decoder_1_out_1[0]));  // open: out_0
  assign Output = In ^ decoder_1_out_1;  // XOr xor_4, 7 bits wide

  // Other names for the same wires on the sheet: I7 = In[0]; I6 = In[1]; I5 = In[2]; I4 = In[3]; I3 = In[4];
  //   I2 = In[5]; I1 = In[6]
endmodule
