// Digital circuit Template.dig as structural Verilog
module Template (
  input  J,
  input  K,
  input  Clear,
  input  Clock,
  output Q,
  output Q_2
);

  wire and_1_out, and_2_out, and_3_out, and_4_out, not_1_out, or_1_out, or_2_out, rs_ff_as_1_nq, rs_ff_as_1_q;

  and and_1 (and_1_out, Q, K, Clock);
  and and_2 (and_2_out, Clock, J, Q_2);
  not not_1 (not_1_out, Clock);
  or or_1 (or_1_out, Clear, and_1_out);
  RS_FF_AS rs_ff_as_1 (.S(and_2_out), .R(or_1_out), .Q(rs_ff_as_1_q), .nQ(rs_ff_as_1_nq));
  and and_3 (and_3_out, rs_ff_as_1_nq, not_1_out);
  and and_4 (and_4_out, not_1_out, rs_ff_as_1_q);
  or or_2 (or_2_out, Clear, and_3_out);
  RS_FF_AS rs_ff_as_2 (.S(and_4_out), .R(or_2_out), .Q(Q), .nQ(Q_2));
endmodule
