// Digital circuit 01.dig as structural Verilog
module _01 (
  input  clk,
  input  reset,
  output C,
  output B,
  output A
);

  wire and_1_out, and_2_out, and_3_out, and_4_out, and_5_out, not_1_out, not_2_out, not_3_out, not_4_out,
       not_5_out, or_1_out;

  and and_1 (and_1_out, not_1_out, not_2_out);
  not not_1 (not_1_out, A);
  not not_2 (not_2_out, C);
  not not_3 (not_3_out, B);
  or or_1 (or_1_out, not_3_out, and_1_out);
  and and_2 (and_2_out, B, not_4_out);
  not not_4 (not_4_out, C);
  not not_5 (not_5_out, reset);
  and and_3 (and_3_out, not_5_out, A);
  and and_4 (and_4_out, not_5_out, or_1_out);
  and and_5 (and_5_out, not_5_out, and_2_out);
  D_FF d_ff_1 (.D(and_3_out), .C(clk), .Q(C));  // open: nQ
  D_FF d_ff_2 (.D(and_4_out), .C(clk), .Q(B));  // open: nQ
  D_FF d_ff_3 (.D(and_5_out), .C(clk), .Q(A));  // open: nQ
endmodule
