// Digital circuit Exam2_1_Template.dig as structural Verilog
module Exam2_1_Template (
  input  X,
  input  Y,
  input  Z,
  input  load,
  input  clock,
  input  reset,
  output A,
  output B,
  output C
);

  wire a_plus, and_1_out, and_2_out, and_3_out, and_4_out, and_5_out, and_6_out, and_7_out, and_8_out,
       and_9_out, and_10_out, and_11_out, b_plus, c_plus, not_1_out, not_2_out, not_3_out, not_4_out,
       not_5_out, not_6_out, not_7_out, or_1_out, or_2_out, or_3_out, or_4_out, or_5_out, or_6_out;

  not not_1 (not_1_out, A);
  not not_2 (not_2_out, C);
  not not_3 (not_3_out, B);
  and and_1 (and_1_out, not_1_out, C);
  and and_2 (and_2_out, A, B, not_2_out);
  and and_3 (and_3_out, A, not_3_out, C);
  and and_4 (and_4_out, A, not_4_out);
  not not_4 (not_4_out, B);
  and and_5 (and_5_out, A, C);
  not not_5 (not_5_out, C);
  or or_1 (or_1_out, and_1_out, and_2_out, and_3_out);
  or or_2 (or_2_out, not_5_out, and_4_out);
  or or_3 (or_3_out, B, and_5_out);
  and and_6 (and_6_out, X, load);
  and and_7 (and_7_out, Y, load);
  and and_8 (and_8_out, Z, load);
  not not_6 (not_6_out, load);
  and and_9 (and_9_out, or_1_out, not_6_out);
  and and_10 (and_10_out, not_6_out, or_2_out);
  and and_11 (and_11_out, not_6_out, or_3_out);
  or or_4 (or_4_out, and_6_out, and_9_out);
  or or_5 (or_5_out, and_7_out, and_10_out);
  or or_6 (or_6_out, and_8_out, and_11_out);
  not not_7 (not_7_out, reset);
  D_FF d_ff_1 (.D(a_plus), .C(clock), .Q(A));  // open: nQ
  D_FF d_ff_2 (.D(b_plus), .C(clock), .Q(B));  // open: nQ
  D_FF d_ff_3 (.D(c_plus), .C(clock), .Q(C));  // open: nQ
  and and_12 (a_plus, or_4_out, not_7_out);
  and and_13 (b_plus, or_5_out, not_7_out);
  and and_14 (c_plus, or_6_out, not_7_out);
endmodule

/* Test case T06:
X Y Z reset load clock A B C
0 0 0 1 0 0 x x x
0 0 0 1 0 1 0 0 0
1 1 0 0 1 0 0 0 0
1 1 0 0 1 1 1 1 0
0 0 0 0 0 0 1 1 0
0 0 0 0 0 1 1 1 1
0 0 0 0 0 0 1 1 1
0 0 0 0 0 1 0 0 1
0 0 0 0 0 0 0 0 1
0 0 0 0 0 1 1 0 0
0 0 0 0 0 0 1 0 0
0 0 0 0 0 1 0 1 0
0 0 0 0 0 0 0 1 0
0 0 0 0 0 1 0 1 1
0 0 0 0 0 0 0 1 1
0 0 0 0 0 1 1 0 1
0 0 0 0 0 0 1 0 1
0 0 0 0 0 1 1 1 1
0 0 0 0 0 0 1 1 1
0 0 0 0 0 1 0 0 1
0 0 0 0 0 0 0 0 1
*/
