// Digital circuit 01.dig as structural Verilog
module _01 (
  input  [7:0] A,
  input  [7:0] B,
  input  start,
  input  clear,
  input  clk,
  output [7:0] \output ,
  output busy
);

  wire a0, a1, a2, a3, a4, a5, a6, a7, and_1_out, and_2_out, and_3_out, loadm, loadn, m_eq__eq_n, m_gt_n,
       multiplexer_3_out, multiplexer_4_out, multiplexer_5_out, or_3_out, Qa, Qb, Qc, reset;
  wire [7:0] m, multiplexer_1_out, multiplexer_2_out, n, sub_1_s, sub_2_s;

  not not_1 (reset, clear);
  Sub #(.Bits(8)) sub_1 (.a(m), .b(n), .c_i(1'b0), .s(sub_1_s));  // open: c_o
  Sub #(.Bits(8)) sub_2 (.a(n), .b(m), .c_i(1'b0), .s(sub_2_s));  // open: c_o
  Comparator #(.Bits(8)) comparator_1 (.a(m), .b(n), .gt(m_gt_n), .eq(m_eq__eq_n));  // open: lt
  Multiplexer #(.Bits(8)) multiplexer_1 (.sel(a3), .in_0(A), .in_1(sub_1_s), .out(multiplexer_1_out));
  Register #(.Bits(8)) register_1 (.D(multiplexer_1_out), .C(clk), .en(loadm), .Q(m));
  Multiplexer #(.Bits(8)) multiplexer_2 (.sel(a2), .in_0(B), .in_1(sub_2_s), .out(multiplexer_2_out));
  Register #(.Bits(8)) register_2 (.D(multiplexer_2_out), .C(clk), .en(loadn), .Q(n));
  Register #(.Bits(8)) register_3 (.D(m), .C(clk), .en(a7), .Q(\output ));
  Multiplexer #(.Selector_Bits(3)) multiplexer_3 (
    .sel({Qa, Qb, Qc}), .in_0(1'b0), .in_1(m_eq__eq_n), .in_2(1'b0), .in_3(1'b0), .in_4(1'b0), .in_5(1'b0),
    .in_6(1'b0), .in_7(1'b0), .out(multiplexer_3_out));
  Decoder #(.Selector_Bits(3)) decoder_1 (
    .sel({Qa, Qb, Qc}), .out_0(a0), .out_1(a1), .out_2(a2), .out_3(a3), .out_4(a4), .out_5(a5), .out_6(a6),
    .out_7(a7));
  and and_1 (and_1_out, reset, multiplexer_3_out);
  D_FF d_ff_1 (.D(and_1_out), .C(clk), .Q(Qa));  // open: nQ
  not not_2 (busy, a0);
  or or_1 (loadm, a3, a0);
  or or_2 (loadn, a2, a0);
  and and_2 (and_2_out, reset, multiplexer_4_out);
  Multiplexer #(.Selector_Bits(3)) multiplexer_4 (
    .sel({Qa, Qb, Qc}), .in_0(1'b0), .in_1(1'b1), .in_2(1'b0), .in_3(1'b0), .in_4(1'b0), .in_5(1'b0),
    .in_6(1'b0), .in_7(1'b0), .out(multiplexer_4_out));
  D_FF d_ff_2 (.D(and_2_out), .C(clk), .Q(Qb));  // open: nQ
  or or_3 (or_3_out, m_eq__eq_n, m_gt_n);
  Multiplexer #(.Selector_Bits(3)) multiplexer_5 (
    .sel({Qa, Qb, Qc}), .in_0(start), .in_1(or_3_out), .in_2(1'b1), .in_3(1'b1), .in_4(1'b0), .in_5(1'b0),
    .in_6(1'b0), .in_7(1'b0), .out(multiplexer_5_out));
  and and_3 (and_3_out, reset, multiplexer_5_out);
  D_FF d_ff_3 (.D(and_3_out), .C(clk), .Q(Qc));  // open: nQ

  // Other names for the same wires on the sheet: gcd[7:0] = \output ; loadgcd = a7; select1 = a3; select2 = a2
endmodule
