// Digital circuit Exam2_2_Template.dig as structural Verilog
module Exam2_2_Template (
  input  reset,
  input  [15:0] P,
  input  start,
  input  clock,
  output [15:0] W,
  output [15:0] H,
  output [31:0] A,
  output busy
);

  wire A0, A1, A2, A3, and_1_out, and_2_out, loadA, loadH, multiplexer_7_out, multiplexer_8_out, not_2_out,
       not_3_out, not_4_out, not_5_out, Qa, Qb, R_eq__eq_0, reset_t, sel;
  wire [15:0] add_1_s, add_2_s, div_1_q, div_2_q, div_2_r, multiplexer_2_out, multiplexer_3_out,
       multiplexer_5_out, multiplexer_6_out, R;
  wire [31:0] mul_1_mul, mul_2_mul, multiplexer_1_out, multiplexer_4_out;

  Add #(.Bits(16)) add_1 (.a(H), .b(16'h1), .c_i(1'b0), .s(add_1_s));  // open: c_o
  Mul #(.Bits(16)) mul_1 (.a(add_1_s), .b(H), .mul(mul_1_mul));
  Mul #(.Bits(16)) mul_2 (.a(H), .b(H), .mul(mul_2_mul));
  Add #(.Bits(16)) add_2 (.a(H), .b(16'h1), .c_i(1'b0), .s(add_2_s));  // open: c_o
  Multiplexer #(.Bits(32)) multiplexer_1 (.sel(sel), .in_0(mul_1_mul), .in_1(mul_2_mul), .out(multiplexer_1_out));
  Div #(.Bits(16)) div_1 (.a(P), .b(16'h2), .q(div_1_q));  // open: r
  Multiplexer #(.Bits(16)) multiplexer_2 (.sel(sel), .in_0(add_2_s), .in_1(H), .out(multiplexer_2_out));
  Div #(.Bits(16)) div_2 (.a(div_1_q), .b(16'h2), .q(div_2_q), .r(div_2_r));
  Multiplexer #(.Bits(16)) multiplexer_3 (
    .sel(reset_t), .in_0({16{1'b0}}), .in_1(multiplexer_2_out), .out(multiplexer_3_out));
  Multiplexer #(.Bits(32)) multiplexer_4 (
    .sel(reset_t), .in_0({32{1'b0}}), .in_1(multiplexer_1_out), .out(multiplexer_4_out));
  Comparator #(.Bits(16)) comparator_1 (.a(R), .b({16{1'b0}}), .eq(R_eq__eq_0));  // open: gt, lt
  not not_1 (reset_t, reset);
  Multiplexer #(.Bits(16)) multiplexer_5 (.sel(reset_t), .in_0({16{1'b0}}), .in_1(div_2_q), .out(multiplexer_5_out));
  Multiplexer #(.Bits(16)) multiplexer_6 (.sel(reset_t), .in_0({16{1'b0}}), .in_1(div_2_r), .out(multiplexer_6_out));
  Register #(.Bits(16)) R_W (.D(multiplexer_3_out), .C(clock), .en(loadA), .Q(W));
  Register #(.Bits(32)) R_A (.D(multiplexer_4_out), .C(clock), .en(loadA), .Q(A));
  Register #(.Bits(16)) R_H (.D(multiplexer_5_out), .C(clock), .en(loadH), .Q(H));
  Register #(.Bits(16)) R_R (.D(multiplexer_6_out), .C(clock), .en(loadH), .Q(R));
  Multiplexer #(.Selector_Bits(2)) multiplexer_7 (
    .sel({Qa, Qb}), .in_0(1'b0), .in_1(1'b1), .in_2(1'b0), .in_3(1'b0), .out(multiplexer_7_out));
  Multiplexer #(.Selector_Bits(2)) multiplexer_8 (
    .sel({Qa, Qb}), .in_0(start), .in_1(R_eq__eq_0), .in_2(1'b0), .in_3(1'b0), .out(multiplexer_8_out));
  and and_1 (and_1_out, reset_t, multiplexer_7_out);
  and and_2 (and_2_out, reset_t, multiplexer_8_out);
  D_FF d_ff_1 (.D(and_1_out), .C(clock), .Q(Qa));  // open: nQ
  D_FF d_ff_2 (.D(and_2_out), .C(clock), .Q(Qb));  // open: nQ
  Decoder #(.Selector_Bits(2)) decoder_1 (.sel({Qa, Qb}), .out_0(A0), .out_1(A1), .out_2(A2), .out_3(A3));
  not not_2 (not_2_out, A0);
  and and_3 (busy, not_2_out, reset_t);
  or or_1 (sel, not_3_out, A3);
  not not_3 (not_3_out, reset_t);
  or or_2 (loadA, A3, not_5_out, A2);
  or or_3 (loadH, not_4_out, start);
  not not_4 (not_4_out, reset_t);
  not not_5 (not_5_out, reset_t);

  // Other names for the same wires on the sheet: clk = clock; loadR = loadH; loadW = loadA
endmodule

/* Test case T01:
P start clock reset W H A busy
0 0 0 1 x x x x
0 0 1 1 x x x x
0 0 0 0 0 0 0 0
0 0 1 0 0 0 0 0
92 1 0 0 x x x x
92 1 1 0 x x x x
0 0 0 0 x x x x
0 0 1 0 x x x x
0 0 0 0 x x x x
0 0 1 0 x x x x
0 0 0 0 x x x x
0 0 1 0 x x x x
0 0 0 0 x x x x
0 0 1 0 x x x x
0 0 0 0 x x x x
0 0 1 0 x x x x
0 0 0 0 x x x x
0 0 1 0 x x x x
0 0 0 0 x x x x
0 0 1 0 x x x x
0 0 0 0 x x x x
0 0 1 0 x x x x
0 0 0 0 x x x x
0 0 1 0 x x x x
0 0 0 0 x x x x
0 0 1 0 x x x x
0 0 0 0 x x x x
0 0 1 0 x x x x
0 0 0 0 x x x x
0 0 1 0 x x x x
0 0 0 0 x x x x
0 0 1 0 x x x x
0 0 0 0 x x x x
0 0 1 0 x x x x
0 0 0 0 x x x x
0 0 1 0 x x x x
0 0 0 0 x x x x
0 0 1 0 x x x x
0 0 0 0 x x x x
0 0 1 0 x x x x
0 0 0 0 x x x x
0 0 1 0 x x x x
0 0 0 0 x x x x
0 0 1 0 x x x x
0 0 0 0 x x x x
0 0 1 0 x x x x
0 0 0 0 x x x x
0 0 1 0 x x x x
0 0 0 0 x x x x
0 0 1 0 x x x x
0 0 0 0 x x x x
0 0 1 0 x x x x
0 0 0 0 x x x x
0 0 1 0 x x x x
0 0 0 0 x x x x
0 0 1 0 x x x x
0 0 0 0 x x x x
0 0 1 0 x x x x
0 0 0 0 x x x x
0 0 1 0 x x x x
0 0 0 0 x x x x
0 0 1 0 x x x x
0 0 0 0 x x x x
0 0 1 0 x x x x
0 0 0 0 x x x x
0 0 1 0 x x x x
0 0 0 0 x x x x
0 0 1 0 x x x x
0 0 0 0 x x x x
0 0 1 0 x x x x
0 0 0 0 x x x x
0 0 1 0 x x x x
0 0 0 0 x x x x
0 0 1 0 x x x x
0 0 0 0 x x x x
0 0 1 0 x x x x
0 0 0 0 x x x x
0 0 1 0 x x x x
0 0 0 0 x x x x
0 0 1 0 x x x x
0 0 0 0 x x x x
0 0 1 0 x x x x
0 0 0 0 x x x x
0 0 1 0 x x x x
0 0 0 0 x x x x
0 0 1 0 x x x x
0 0 0 0 x x x x
0 0 1 0 x x x x
0 0 0 0 x x x x
0 0 1 0 x x x x
0 0 0 0 x x x x
0 0 1 0 x x x x
0 0 0 0 x x x x
0 0 1 0 x x x x
0 0 0 0 x x x x
0 0 1 0 x x x x
0 0 0 0 x x x x
0 0 1 0 x x x x
0 0 0 0 x x x x
0 0 1 0 x x x x
0 0 0 0 x x x x
0 0 1 0 x x x x
0 0 0 0 x x x x
0 0 1 0 x x x x
0 0 0 0 x x x x
0 0 1 0 x x x x
0 0 0 0 x x x x
0 0 1 0 x x x x
0 0 0 0 x x x x
0 0 1 0 x x x x
0 0 0 0 x x x x
0 0 1 0 x x x x
0 0 0 0 x x x x
0 0 1 0 x x x x
0 0 0 0 x x x x
0 0 1 0 x x x x
0 0 0 0 x x x x
0 0 1 0 x x x x
0 0 0 0 x x x x
0 0 1 0 x x x x
0 0 0 0 x x x x
0 0 1 0 x x x x
0 0 0 0 x x x x
0 0 1 0 x x x x
0 0 0 0 x x x x
0 0 1 0 x x x x
0 0 0 0 x x x x
0 0 1 0 x x x x
0 0 0 0 x x x x
0 0 1 0 x x x x
0 0 0 0 x x x x
0 0 1 0 x x x x
0 0 0 0 x x x x
0 0 1 0 x x x x
0 0 0 0 x x x x
0 0 1 0 x x x x
0 0 0 0 x x x x
0 0 1 0 x x x x
0 0 0 0 x x x x
0 0 1 0 x x x x
0 0 0 0 x x x x
0 0 1 0 x x x x
0 0 0 0 x x x x
0 0 1 0 x x x x
0 0 0 0 x x x x
0 0 1 0 x x x x
0 0 0 0 x x x x
0 0 1 0 x x x x
0 0 0 0 x x x x
0 0 1 0 x x x x
0 0 0 0 x x x x
0 0 1 0 x x x x
0 0 0 0 x x x x
0 0 1 0 x x x x
0 0 0 0 x x x x
0 0 1 0 x x x x
0 0 0 0 x x x x
0 0 1 0 x x x x
0 0 0 0 x x x x
0 0 1 0 x x x x
0 0 0 0 x x x x
0 0 1 0 x x x x
0 0 0 0 x x x x
0 0 1 0 x x x x
0 0 0 0 x x x x
0 0 1 0 x x x x
0 0 0 0 x x x x
0 0 1 0 x x x x
0 0 0 0 x x x x
0 0 1 0 x x x x
0 0 0 0 x x x x
0 0 1 0 x x x x
0 0 0 0 x x x x
0 0 1 0 x x x x
0 0 0 0 x x x x
0 0 1 0 x x x x
0 0 0 0 x x x x
0 0 1 0 x x x x
0 0 0 0 x x x x
0 0 1 0 x x x x
0 0 0 0 x x x x
0 0 1 0 x x x x
0 0 0 0 x x x x
0 0 1 0 x x x x
0 0 0 0 x x x x
0 0 1 0 x x x x
0 0 0 0 x x x x
0 0 1 0 x x x x
0 0 0 0 x x x x
0 0 1 0 x x x x
0 0 0 0 x x x x
0 0 1 0 x x x x
0 0 0 0 x x x x
0 0 1 0 x x x x
0 0 0 0 x x x x
0 0 1 0 x x x x
0 0 0 0 x x x x
0 0 1 0 x x x x
0 0 0 0 x x x x
0 0 1 0 x x x x
0 0 0 0 x x x x
0 0 1 0 x x x x
0 0 0 0 x x x x
0 0 1 0 x x x x
0 0 0 0 x x x x
0 0 1 0 x x x x
0 0 0 0 x x x x
0 0 1 0 x x x x
0 0 0 0 x x x x
0 0 1 0 x x x x
0 0 0 0 x x x x
0 0 1 0 x x x x
0 0 0 0 x x x x
0 0 1 0 x x x x
0 0 0 0 x x x x
0 0 1 0 x x x x
0 0 0 0 x x x x
0 0 1 0 x x x x
0 0 0 0 x x x x
0 0 1 0 x x x x
0 0 0 0 x x x x
0 0 1 0 x x x x
0 0 0 0 x x x x
0 0 1 0 x x x x
0 0 0 0 x x x x
0 0 1 0 x x x x
0 0 0 0 x x x x
0 0 1 0 x x x x
0 0 0 0 x x x x
0 0 1 0 x x x x
0 0 0 0 x x x x
0 0 1 0 x x x x
0 0 0 0 x x x x
0 0 1 0 x x x x
0 0 0 0 x x x x
0 0 1 0 x x x x
0 0 0 0 x x x x
0 0 1 0 x x x x
0 0 0 0 x x x x
0 0 1 0 x x x x
0 0 0 0 x x x x
0 0 1 0 x x x x
0 0 0 0 x x x x
0 0 1 0 x x x x
0 0 0 0 x x x x
0 0 1 0 x x x x
0 0 0 0 x x x x
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*/
